// Logisim project p1.circ as structural Verilog: 1 circuit, main circuit main
module main (
  input  X,
  input  Y,
  output Output
);

  wire transistor_2_out;

  Transistor #(.\type ("n")) transistor_1 (.in(1'b0), .out(Output), .gate(X));
  Transistor transistor_2 (.in(1'b1), .out(transistor_2_out), .gate(X));
  Transistor transistor_3 (.in(transistor_2_out), .out(Output), .gate(Y));
  Transistor #(.\type ("n")) transistor_4 (.in(1'b0), .out(Output), .gate(Y));

  // Notes on the sheet:
  //   Fig. NOR Gate
endmodule
