// Logisim project p2.circ as structural Verilog: 1 circuit, main circuit main
module main (
  input  X,
  input  Y,
  output Output
);

  wire transistor_4_out;

  Transistor transistor_1 (.in(1'b1), .out(Output), .gate(X));
  Transistor transistor_2 (.in(1'b1), .out(Output), .gate(Y));
  Transistor #(.\type ("n")) transistor_3 (.in(transistor_4_out), .out(Output), .gate(X));
  Transistor #(.\type ("n")) transistor_4 (.in(1'b0), .out(transistor_4_out), .gate(Y));

  // Notes on the sheet:
  //   Fig. NAND Gate
endmodule
