// Logisim project p3.circ as structural Verilog: 1 circuit, main circuit main
module main (
  input  X,
  input  Y,
  output Output
);

  wire transistor_1_out;

  Transistor transistor_1 (.in(1'b1), .out(transistor_1_out), .gate(X));
  Transistor #(.\type ("n")) transistor_2 (.in(1'b0), .out(transistor_1_out), .gate(X));
  Transistor transistor_3 (.in(X), .out(Output), .gate(Y));
  Transistor #(.\type ("n")) transistor_4 (.in(transistor_1_out), .out(Output), .gate(Y));

  // Notes on the sheet:
  //   Fig. XOR Gate
endmodule
