// Logisim project p4.circ as structural Verilog: 1 circuit, main circuit main
module main (
  input  X,
  input  Y,
  input  Z,
  output Output
);

  wire transistor_2_out, transistor_3_out;

  Transistor transistor_1 (.in(1'b0), .out(Output), .gate(X));
  Transistor #(.\type ("n")) transistor_2 (.in(1'b1), .out(transistor_2_out), .gate(X));
  Transistor #(.\type ("n")) transistor_3 (.in(transistor_2_out), .out(transistor_3_out), .gate(Y));
  Transistor #(.\type ("n")) transistor_4 (.in(transistor_3_out), .out(Output), .gate(Z));
  Transistor transistor_5 (.in(1'b0), .out(Output), .gate(Y));
  Transistor transistor_6 (.in(1'b0), .out(Output), .gate(Z));

  // Notes on the sheet:
  //   Fig. 3-Input AND Gate
endmodule
