// Logisim project p5.circ as structural Verilog: 1 circuit, main circuit main
module main (
  input  A,
  input  B,
  input  C,
  input  D,
  output out_5
);

  wire transistor_2_out, transistor_3_out, transistor_4_out;

  Transistor transistor_1 (.in(transistor_2_out), .out(out_5), .gate(D));
  Transistor transistor_2 (.in(transistor_3_out), .out(transistor_2_out), .gate(C));
  Transistor transistor_3 (.in(transistor_4_out), .out(transistor_3_out), .gate(B));
  Transistor transistor_4 (.in(1'b0), .out(transistor_4_out), .gate(A));
  Transistor #(.\type ("n")) transistor_5 (.in(1'b1), .out(out_5), .gate(A));
  Transistor #(.\type ("n")) transistor_6 (.in(1'b1), .out(out_5), .gate(B));
  Transistor #(.\type ("n")) transistor_7 (.in(1'b1), .out(out_5), .gate(C));
  Transistor #(.\type ("n")) transistor_8 (.in(1'b1), .out(out_5), .gate(D));

  // Notes on the sheet:
  //   Fig. 4-Inputt OR Gate
endmodule
