// Logisim project L10Q1_D.circ as structural Verilog: 1 circuit, main circuit main
module main (
  input  C0,
  input  C1,
  output S1,
  output S0,
  output D0,
  output D1
);

  wire and_1_out, and_2_out, and_3_out, and_4_out, and_5_out, and_6_out, clock_1_out, not_1_out, not_2_out,
       not_3_out, not_4_out, not_5_out, xnor_1_out, xor_1_out;

  not not_1 (not_1_out, S0);
  Clock clock_1 (.out(clock_1_out));
  xnor xnor_1 (xnor_1_out, C1, C0);
  xor xor_1 (xor_1_out, C1, C0);
  D_Flip_Flop d_ff_1 (.clk(clock_1_out), .D(D1), .Q(S1));  // open: Qn, preset, en, reset
  and and_1 (and_1_out, S0, xnor_1_out);
  or or_1 (D0, and_1_out, and_2_out);
  and and_2 (and_2_out, not_1_out, xor_1_out);
  D_Flip_Flop d_ff_2 (.clk(clock_1_out), .D(D0), .Q(S0));  // open: Qn, preset, en, reset
  not not_2 (not_2_out, S1);
  not not_3 (not_3_out, S0);
  not not_4 (not_4_out, C1);
  not not_5 (not_5_out, C0);
  Hex_Digit_Display hex_digit_display_1 (.value({2'b00, S1, S0}));  // open: dp
  and and_3 (and_3_out, S1, not_4_out, S0);
  and and_4 (and_4_out, C1, S0, not_2_out);
  and and_5 (and_5_out, not_2_out, C0, not_3_out);
  and and_6 (and_6_out, not_3_out, S1, not_5_out);
  or or_2 (D1, and_3_out, and_4_out, and_5_out, and_6_out);

  // Notes on the sheet:
  //   C0 C1  Operation
  //   0    0   Stop Counting
  //   0    1   Count up by one 
  //   1    0   Count down by one
  //   1    1   Count by two 
  //   Fig.  Described counter Using D-flipflop
endmodule
