// Logisim project L10Q1_JK.circ as structural Verilog: 1 circuit, main circuit main
module main (
  input  C0,
  input  C1,
  output S1,
  output S0,
  output K0,
  output K1,
  output J0,
  output J1
);

  wire and_1_out, and_2_out, clock_1_out, not_1_out;

  Clock clock_1 (.out(clock_1_out));
  xor xor_1 (J0, C1, C0);
  J_K_Flip_Flop j_k_ff_1 (.J(J1), .clk(clock_1_out), .K(J1), .Q(S1));  // open: Qn, preset, en, reset
  J_K_Flip_Flop j_k_ff_2 (.J(J0), .clk(clock_1_out), .K(J0), .Q(S0));  // open: Qn, preset, en, reset
  not not_1 (not_1_out, S0);
  Hex_Digit_Display hex_digit_display_1 (.value({2'b00, S1, S0}));  // open: dp
  and and_1 (and_1_out, S0, C1);
  or or_1 (J1, and_1_out, and_2_out);
  and and_2 (and_2_out, not_1_out, C0);

  assign K0 = J0;
  assign K1 = J1;

  // Notes on the sheet:
  //   C0 C1  Operation
  //   0    0   Stop Counting
  //   0    1   Count up by one 
  //   1    0   Count down by one
  //   1    1   Count by two 
  //   Fig.  Described counter Using JK-flipflop
endmodule
