// Logisim project L10Q1_SR.circ as structural Verilog: 1 circuit, main circuit main
module main (
  input  C0,
  input  C1,
  output St1,
  output St0,
  output R0,
  output R1,
  output S0,
  output S1
);

  wire and_3_out, and_4_out, and_5_out, and_6_out, clock_1_out, not_1_out, not_2_out, not_3_out, xor_1_out;

  not not_1 (not_1_out, St0);
  Clock clock_1 (.out(clock_1_out));
  xor xor_1 (xor_1_out, C1, C0);
  S_R_Flip_Flop s_r_ff_1 (.S(S1), .clk(clock_1_out), .R(R1), .Q(St1));  // open: Qn, preset, reset, en
  and and_1 (R0, St0, xor_1_out);
  and and_2 (S0, xor_1_out, not_1_out);
  S_R_Flip_Flop s_r_ff_2 (.S(S0), .clk(clock_1_out), .R(R0), .Q(St0));  // open: Qn, preset, reset, en
  not not_2 (not_2_out, St1);
  not not_3 (not_3_out, St0);
  Hex_Digit_Display hex_digit_display_1 (.value({2'b00, St1, St0}));  // open: dp
  and and_3 (and_3_out, C1, St1, St0);
  or or_1 (R1, and_3_out, and_4_out);
  and and_4 (and_4_out, C0, St1, not_3_out);
  and and_5 (and_5_out, St0, not_2_out, C1);
  or or_2 (S1, and_5_out, and_6_out);
  and and_6 (and_6_out, not_2_out, C0, not_3_out);

  // Notes on the sheet:
  //   C0 C1  Operation
  //   0    0   Stop Counting
  //   0    1   Count up by one 
  //   1    0   Count down by one
  //   1    1   Count by two 
  //   Fig.  Described counter Using SR-flipflop
endmodule
