// Logisim project L10Q1_T.circ as structural Verilog: 1 circuit, main circuit main
module main (
  input  C0,
  input  C1,
  output S1,
  output S0,
  output T0,
  output T1
);

  wire and_1_out, and_2_out, clock_1_out, not_1_out;

  xor xor_1 (T0, C1, C0);
  Clock clock_1 (.out(clock_1_out));
  T_Flip_Flop t_ff_1 (.clk(clock_1_out), .T(T1), .Q(S1));  // open: Qn, preset, reset, en
  T_Flip_Flop t_ff_2 (.clk(clock_1_out), .T(T0), .Q(S0));  // open: Qn, preset, reset, en
  not not_1 (not_1_out, S0);
  Hex_Digit_Display hex_digit_display_1 (.value({2'b00, S1, S0}));  // open: dp
  and and_1 (and_1_out, S0, C1);
  and and_2 (and_2_out, not_1_out, C0);
  or or_1 (T1, and_1_out, and_2_out);

  // Notes on the sheet:
  //   C0 C1  Operation
  //   0    0   Stop Counting
  //   0    1   Count up by one 
  //   1    0   Count down by one
  //   1    1   Count by two 
  //   Fig.  Described counter Using T-flipflop
endmodule
