// Logisim project L10Q2.circ as structural Verilog: 1 circuit, main circuit main
module main (
  input  in_1
);

  wire A_out, adder_1_cout, adder_1_out, B_out, CLK_out, d_ff_1_q;

  Clock CLK (.out(CLK_out));
  Shift_Register A (
    .clk(CLK_out), .out(A_out));  // open: shift, in, load, clr, d0, q0, d1, q1, d2, q2, d3, q3, d4, q4, d5, q5, d6, q6, d7, q7
  Shift_Register B (
    .clk(CLK_out), .out(B_out));  // open: shift, in, load, clr, d0, q0, d1, q1, d2, q2, d3, q3, d4, q4, d5, q5, d6, q6, d7, q7
  Adder #(.width(1)) adder_1 (.a(A_out), .b(B_out), .out(adder_1_out), .cin(d_ff_1_q), .cout(adder_1_cout));
  D_Flip_Flop d_ff_1 (.clk(CLK_out), .D(adder_1_cout), .Q(d_ff_1_q), .reset(in_1));  // open: Qn, preset, en
  Shift_Register Y (
    .in(adder_1_out), .clk(CLK_out));  // open: shift, out, load, clr, d0, q0, d1, q1, d2, q2, d3, q3, d4, q4, d5, q5, d6, q6, d7, q7

  // Notes on the sheet:
  //   Fig. 8-bit Full Adder using 1-bit full adder and shift registers
endmodule
