// Logisim project L10Q3.circ as structural Verilog: 1 circuit, main circuit main
module main (
  output [3:0] out_1,
  output C4,
  output C3,
  output C2,
  output C1
);

  wire clock_1_out, nor_1_out, xor_1_out, xor_2_out, xor_3_out, xor_4_out;

  nor nor_1 (nor_1_out, C1, C2);
  xor xor_1 (xor_1_out, 1'b1, C4);
  D_Flip_Flop d_ff_1 (.clk(nor_1_out), .D(xor_1_out), .Q(C4));  // open: Qn, preset, en, reset
  D_Flip_Flop d_ff_2 (.clk(nor_1_out), .D(xor_2_out), .Q(C3));  // open: Qn, preset, en, reset
  xor xor_2 (xor_2_out, C4, C3);
  Hex_Digit_Display hex_digit_display_1 (.value({C3, C4, C1, C2}));  // open: dp
  Clock clock_1 (.out(clock_1_out));
  xor xor_3 (xor_3_out, 1'b1, C2);
  D_Flip_Flop d_ff_3 (.clk(clock_1_out), .D(xor_3_out), .Q(C2));  // open: Qn, preset, en, reset
  xor xor_4 (xor_4_out, C2, C1);
  D_Flip_Flop d_ff_4 (.clk(clock_1_out), .D(xor_4_out), .Q(C1));  // open: Qn, preset, en, reset

  assign out_1 = {C3, C4, C1, C2};

  // Notes on the sheet:
  //   Fig. 4-bit counter using 2-bit counters
endmodule
