// Logisim project L11Q1.circ as structural Verilog: 1 circuit, main circuit main
module main (
  input  [1:0] C0_C1,
  output [3:0] out_2
);

  wire clock_1_out, decoder_1_out0, decoder_1_out1, decoder_1_out2, decoder_1_out3;
  wire [3:0] multiplexer_1_out, multiplexer_2_out, multiplexer_3_out, multiplexer_4_out, multiplexer_5_out;

  Decoder #(.select(2)) decoder_1 (
    .out0(decoder_1_out0), .out1(decoder_1_out1), .out2(decoder_1_out2), .out3(decoder_1_out3), .sel(C0_C1));  // open: en
  Multiplexer #(.select(4), .width(4)) multiplexer_1 (
    .in0(4'b0000), .in1(4'b0001), .in2(4'b0010), .in3(4'b0011), .in4(4'b0100), .in5(4'b0101), .in6(4'b0110),
    .in7(4'b0111), .in8(4'b1000), .in9(4'b1001), .in10(4'b1010), .in11(4'b1011), .in12(4'b1100),
    .in13(4'b1101), .in14(4'b1110), .in15(4'b1111), .out(multiplexer_1_out), .sel(out_2), .en(decoder_1_out0));
  Multiplexer #(.select(4), .width(4)) multiplexer_2 (
    .in0(4'b1110), .in1(4'b1111), .in2(4'b0000), .in3(4'b0001), .in4(4'b0010), .in5(4'b0011), .in6(4'b0100),
    .in7(4'b0101), .in8(4'b0110), .in9(4'b0111), .in10(4'b1000), .in11(4'b1001), .in12(4'b1010),
    .in13(4'b1011), .in14(4'b1100), .in15(4'b1101), .out(multiplexer_2_out), .sel(out_2), .en(decoder_1_out2));
  Multiplexer #(.select(4), .width(4)) multiplexer_3 (
    .in0(4'b0001), .in1(4'b0010), .in2(4'b0011), .in3(4'b0100), .in4(4'b0101), .in5(4'b0110), .in6(4'b0111),
    .in7(4'b1000), .in8(4'b1001), .in9(4'b1010), .in10(4'b1011), .in11(4'b1100), .in12(4'b1101),
    .in13(4'b1110), .in14(4'b1111), .in15(4'b0000), .out(multiplexer_3_out), .sel(out_2), .en(decoder_1_out1));
  Multiplexer #(.select(4), .width(4)) multiplexer_4 (
    .in0(4'b0011), .in1(4'b0100), .in2(4'b0101), .in3(4'b0110), .in4(4'b0111), .in5(4'b1000), .in6(4'b1001),
    .in7(4'b1010), .in8(4'b1011), .in9(4'b1100), .in10(4'b1101), .in11(4'b1110), .in12(4'b1111),
    .in13(4'b0000), .in14(4'b0001), .in15(4'b0010), .out(multiplexer_4_out), .sel(out_2), .en(decoder_1_out3));
  Multiplexer #(.select(2), .width(4)) multiplexer_5 (
    .in0(multiplexer_1_out), .in1(multiplexer_3_out), .in2(multiplexer_2_out), .in3(multiplexer_4_out),
    .out(multiplexer_5_out), .sel(C0_C1));  // open: en
  Register #(.width(4)) register_1 (.D(multiplexer_5_out), .Q(out_2), .clk(clock_1_out));  // open: en, clr
  Clock clock_1 (.out(clock_1_out));
  Hex_Digit_Display hex_digit_display_1 (.value(out_2));  // open: dp

  // Notes on the sheet:
  //   C0    C1    Operation
  //   0       0     Stop Counting
  //   0       1   Count up by one
  //   1        0    Count down by two
  //   1       1     Count up by three
endmodule
