// Logisim project L11Q2_J-K-mealy.circ as structural Verilog: 1 circuit, main circuit main
module main (
  input  I0__input,
  input  Reset,
  output C1,
  output C0,
  output O__output
);

  wire Clock_out, J0, J1, K0, not_1_out, not_2_out;

  Clock Clock (.out(Clock_out));
  J_K_Flip_Flop j_k_ff_1 (.J(J1), .clk(Clock_out), .K(C0), .Q(C1), .reset(Reset));  // open: Qn, preset, en
  J_K_Flip_Flop j_k_ff_2 (.J(J0), .clk(Clock_out), .K(K0), .Q(C0), .reset(Reset));  // open: Qn, preset, en
  and and_1 (J1, I0__input, C0);
  xor xor_1 (J0, C1, I0__input);
  not not_1 (not_1_out, I0__input);
  or or_1 (K0, not_1_out, not_2_out);
  not not_2 (not_2_out, C1);
  and and_2 (O__output, C1, C0, I0__input);

  // Other names for the same wires on the sheet: I0 = I0__input; K1 = C0

  // Notes on the sheet:
  //   Fig. (1101) Mealy FSM detector using JK Flipflop
endmodule
