// Logisim project L11Q2_J-K-moore.circ as structural Verilog: 1 circuit, main circuit main
module main (
  input  I0__input,
  input  Reset,
  output C2,
  output C1,
  output C0,
  output O__output
);

  wire and_2_out, and_3_out, and_4_out, and_5_out, Clock_out, J0, J1, J2, not_1_out, not_2_out, not_3_out;

  Clock Clock (.out(Clock_out));
  J_K_Flip_Flop j_k_ff_1 (.J(J2), .clk(Clock_out), .K(1'b1), .Q(C2), .reset(Reset));  // open: Qn, preset, en
  J_K_Flip_Flop j_k_ff_2 (.J(J1), .clk(Clock_out), .K(C0), .Q(C1), .reset(Reset));  // open: Qn, preset, en
  not not_1 (not_1_out, C2);
  and and_1 (J2, I0__input, C1, C0);
  and and_2 (and_2_out, C2, I0__input);
  and and_3 (and_3_out, C0, I0__input);
  not not_2 (not_2_out, I0__input);
  and and_4 (and_4_out, not_2_out, C1);
  not not_3 (not_3_out, C1);
  and and_5 (and_5_out, not_3_out, not_1_out, I0__input);
  J_K_Flip_Flop j_k_ff_3 (.J(J0), .clk(Clock_out), .K(1'b1), .Q(C0), .reset(Reset));  // open: Qn, preset, en
  or or_1 (J1, and_2_out, and_3_out);
  or or_2 (J0, and_4_out, and_5_out);

  assign O__output = C2;

  // Other names for the same wires on the sheet: I0 = I0__input; K1 = C0

  // Notes on the sheet:
  //   Fig. (1101) Moore FSM detector using JK Flipflop 
endmodule
