// Logisim project L11Q2_T-mealy.circ as structural Verilog: 1 circuit, main circuit main
module main (
  input  I0__input,
  input  Reset,
  output C1,
  output C0,
  output O__output
);

  wire and_1_out, and_2_out, and_3_out, Clock_out, not_1_out, T0, T1, xor_1_out;

  Clock Clock (.out(Clock_out));
  T_Flip_Flop t_ff_1 (.clk(Clock_out), .T(T1), .Q(C1), .reset(Reset));  // open: Qn, preset, en
  T_Flip_Flop t_ff_2 (.clk(Clock_out), .T(T0), .Q(C0), .reset(Reset));  // open: Qn, preset, en
  and and_1 (and_1_out, I0__input, C0);
  and and_2 (and_2_out, C1, C0);
  xor xor_1 (xor_1_out, C1, I0__input);
  and and_3 (and_3_out, C0, not_1_out);
  not not_1 (not_1_out, C1);
  or or_1 (T1, and_1_out, and_2_out);
  or or_2 (T0, xor_1_out, and_3_out);
  and and_4 (O__output, C1, C0, I0__input);

  // Other names for the same wires on the sheet: I0 = I0__input

  // Notes on the sheet:
  //   Fig. (1101) Mealy FSM detector using T Flipflop
endmodule
