// Logisim project L11Q2_T-moore.circ as structural Verilog: 1 circuit, main circuit main
module main (
  input  I0__input,
  input  Reset,
  output C2,
  output C1,
  output C0,
  output O__output
);

  wire and_1_out, and_2_out, and_3_out, and_4_out, and_5_out, and_6_out, Clock_out, not_1_out, not_2_out,
       not_3_out, T0, T1, T2;

  Clock Clock (.out(Clock_out));
  T_Flip_Flop t_ff_1 (.clk(Clock_out), .T(T2), .Q(C2), .reset(Reset));  // open: Qn, preset, en
  T_Flip_Flop t_ff_2 (.clk(Clock_out), .T(T1), .Q(C1), .reset(Reset));  // open: Qn, preset, en
  and and_1 (and_1_out, I0__input, C1, C0);
  and and_2 (and_2_out, C2, I0__input);
  and and_3 (and_3_out, C1, C0);
  and and_4 (and_4_out, I0__input, C0);
  not not_1 (not_1_out, I0__input);
  not not_2 (not_2_out, C1);
  not not_3 (not_3_out, C2);
  T_Flip_Flop t_ff_3 (.clk(Clock_out), .T(T0), .Q(C0), .reset(Reset));  // open: Qn, preset, en
  or or_1 (T2, and_1_out, C2);
  or or_2 (T1, and_2_out, and_3_out, and_4_out);
  and and_5 (and_5_out, C1, not_1_out);
  and and_6 (and_6_out, not_2_out, not_3_out, I0__input);
  or or_3 (T0, and_5_out, and_6_out, C0);

  assign O__output = C2;

  // Other names for the same wires on the sheet: I0 = I0__input

  // Notes on the sheet:
  //   Fig. (1101) Moore FSM detector using T Flipflop 
endmodule
