// Logisim project L11Q3.circ as structural Verilog: 1 circuit, main circuit main
module main (
  input  [7:0] Input_Temperature,
  output [7:0] Average_Temperature
);

  wire clock_1_out;
  wire [7:0] adder_1_out, adder_2_out, adder_3_out, register_1_q, register_2_q, register_3_q, register_4_q;

  Clock clock_1 (.out(clock_1_out));
  Register register_1 (.D(Input_Temperature), .Q(register_1_q), .clk(clock_1_out));  // open: en, clr
  Register register_2 (.D(register_1_q), .Q(register_2_q), .clk(clock_1_out));  // open: en, clr
  Register register_3 (.D(register_2_q), .Q(register_3_q), .clk(clock_1_out));  // open: en, clr
  Adder adder_1 (.a(register_1_q), .b(register_2_q), .out(adder_1_out));  // open: cin, cout
  Register register_4 (.D(register_3_q), .Q(register_4_q), .clk(clock_1_out));  // open: en, clr
  Adder adder_2 (.a(register_3_q), .b(register_4_q), .out(adder_2_out));  // open: cin, cout
  Adder adder_3 (.a(adder_2_out), .b(adder_1_out), .out(adder_3_out));  // open: cin, cout
  Shifter #(.shift("lr")) shifter_1 (.in(adder_3_out), .\dist (3'b010), .out(Average_Temperature));

  // Notes on the sheet:
  //   Fig. Average Temperature Calculator
endmodule
