// Logisim project p3_logisim.circ as structural Verilog: 2 circuits, main circuit main
module main (
  input  [7:0] Input_1,
  input  [7:0] Input_2,
  input  [1:0] OPR,
  output Zero_Flag,
  output [7:0] Output,
  output [7:0] operation_out
);

  wire CLOCK, decoder_1_out1, decoder_1_out2, decoder_1_out3, decoder_1_out4, decoder_1_out5, decoder_1_out6,
       decoder_1_out7;
  wire [1:0] curr_state, next_state;
  wire [2:0] SELA, SELB, SELD;
  wire [7:0] multiplexer_4_out, multiplexer_5_out, R1_q, R2_q, R3_q, R4_q, R5_q, R6_q;

  Decoder #(.select(3)) decoder_1 (
    .out1(decoder_1_out1), .out2(decoder_1_out2), .out3(decoder_1_out3), .out4(decoder_1_out4),
    .out5(decoder_1_out5), .out6(decoder_1_out6), .out7(decoder_1_out7), .sel(SELD));  // open: out0, en
  Multiplexer #(.select(2), .width(3)) multiplexer_1 (
    .in0(3'b000), .in1(3'b100), .in2(3'b001), .in3(3'b100), .out(SELA), .sel(curr_state));  // open: en
  Clock clock_1 (.out(CLOCK));
  Register R1 (.D(Output), .en(decoder_1_out1), .Q(R1_q), .clk(CLOCK));  // open: clr
  Register R2 (.D(Output), .en(decoder_1_out2), .Q(R2_q), .clk(CLOCK));  // open: clr
  Register R3 (.D(Output), .en(decoder_1_out3), .Q(R3_q), .clk(CLOCK));  // open: clr
  Register R4 (.D(Output), .en(decoder_1_out4), .Q(R4_q), .clk(CLOCK));  // open: clr
  Register R5 (.D(Output), .en(decoder_1_out5), .Q(R5_q), .clk(CLOCK));  // open: clr
  Register R6 (.D(Output), .en(decoder_1_out6), .Q(R6_q), .clk(CLOCK));  // open: clr
  Register R7 (.D(Output), .en(decoder_1_out7), .Q(operation_out), .clk(CLOCK));  // open: clr
  Multiplexer #(.select(2), .width(3)) multiplexer_2 (
    .in0(3'b100), .in1(3'b000), .in2(3'b010), .in3(3'b100), .out(SELB), .sel(curr_state));  // open: en
  Register #(.width(2)) register_1 (.D(next_state), .Q(curr_state), .clk(CLOCK));  // open: en, clr
  Multiplexer #(.select(2), .width(3)) multiplexer_3 (
    .in0(3'b001), .in1(3'b010), .in2(3'b111), .in3(3'b100), .out(SELD), .sel(curr_state));  // open: en
  Multiplexer #(.select(3), .width(8)) multiplexer_4 (
    .in0(Input_1), .in1(R1_q), .in2(R2_q), .in3(R3_q), .in4(R4_q), .in5(R5_q), .in6(R6_q),
    .in7(operation_out), .out(multiplexer_4_out), .sel(SELA));  // open: en
  Multiplexer #(.select(3), .width(8)) multiplexer_5 (
    .in0(Input_2), .in1(R1_q), .in2(R2_q), .in3(R3_q), .in4(R4_q), .in5(R5_q), .in6(R6_q),
    .in7(operation_out), .out(multiplexer_5_out), .sel(SELB));  // open: en
  _8bit_ALU u_8bit_alu_1 (.A(multiplexer_4_out), .B(multiplexer_5_out), .Opcode(OPR), .F(Zero_Flag), .Output(Output));
  Multiplexer #(.select(2), .width(2)) multiplexer_6 (
    .in0(2'b01), .in1(2'b10), .in2(2'b00), .in3(2'b00), .out(next_state), .sel(curr_state));  // open: en
endmodule

// ALU
module _8bit_ALU (
  input  [7:0] A,
  input  [7:0] B,
  input  [1:0] Opcode,
  output F,
  output [7:0] Output
);

  wire [7:0] adder_1_out, and_1_out, subtractor_1_out, xor_1_out;

  Adder adder_1 (.a(A), .b(B), .out(adder_1_out), .cin(1'b0));  // open: cout
  Subtractor subtractor_1 (.a(A), .b(B), .out(subtractor_1_out), .bin(1'b0));  // open: bout
  assign and_1_out = A & B;  // AND_Gate and_1, 8 bits wide
  assign xor_1_out = A ^ B;  // XOR_Gate xor_1, 8 bits wide
  Multiplexer #(.select(2), .width(8)) multiplexer_1 (
    .in0(adder_1_out), .in1(subtractor_1_out), .in2(and_1_out), .in3(xor_1_out), .out(Output), .sel(Opcode));  // open: en
  Comparator comparator_1 (.a({8{1'b0}}), .b(Output), .eq(F));  // open: gt, lt

  // Notes on the sheet:
  //   Fig. 8-bit ALU
endmodule
