// Logisim project Gates.circ as structural Verilog: 6 circuits, main circuit nor2
module nor2 (
  input  X,
  input  Y,
  output Output
);

  wire transistor_2_out;

  Transistor #(.\type ("n")) transistor_1 (.in(1'b0), .out(Output), .gate(X));
  Transistor transistor_2 (.in(1'b1), .out(transistor_2_out), .gate(X));
  Transistor transistor_3 (.in(transistor_2_out), .out(Output), .gate(Y));
  Transistor #(.\type ("n")) transistor_4 (.in(1'b0), .out(Output), .gate(Y));

  // Notes on the sheet:
  //   Fig. NOR Gate
endmodule

module nand2 (
  input  X,
  input  Y,
  output Output
);

  wire transistor_4_out;

  Transistor transistor_1 (.in(1'b1), .out(Output), .gate(X));
  Transistor transistor_2 (.in(1'b1), .out(Output), .gate(Y));
  Transistor #(.\type ("n")) transistor_3 (.in(transistor_4_out), .out(Output), .gate(X));
  Transistor #(.\type ("n")) transistor_4 (.in(1'b0), .out(transistor_4_out), .gate(Y));

  // Notes on the sheet:
  //   Fig. NAND Gate
endmodule

module xor2 (
  input  X,
  input  Y,
  output Output
);

  wire transistor_1_out;

  Transistor transistor_1 (.in(1'b1), .out(transistor_1_out), .gate(X));
  Transistor #(.\type ("n")) transistor_2 (.in(1'b0), .out(transistor_1_out), .gate(X));
  Transistor transistor_3 (.in(X), .out(Output), .gate(Y));
  Transistor #(.\type ("n")) transistor_4 (.in(transistor_1_out), .out(Output), .gate(Y));

  // Notes on the sheet:
  //   Fig. XOR Gate
endmodule

module and3 (
  input  X,
  input  Y,
  input  Z,
  output Output
);

  wire transistor_2_out, transistor_3_out;

  Transistor transistor_1 (.in(1'b0), .out(Output), .gate(X));
  Transistor #(.\type ("n")) transistor_2 (.in(1'b1), .out(transistor_2_out), .gate(X));
  Transistor #(.\type ("n")) transistor_3 (.in(transistor_2_out), .out(transistor_3_out), .gate(Y));
  Transistor #(.\type ("n")) transistor_4 (.in(transistor_3_out), .out(Output), .gate(Z));
  Transistor transistor_5 (.in(1'b0), .out(Output), .gate(Y));
  Transistor transistor_6 (.in(1'b0), .out(Output), .gate(Z));

  // Notes on the sheet:
  //   Fig. 3-Input AND Gate
endmodule

module or4 (
  input  A,
  input  B,
  input  C,
  input  D,
  output out_5
);

  wire transistor_2_out, transistor_3_out, transistor_4_out;

  Transistor transistor_1 (.in(transistor_2_out), .out(out_5), .gate(D));
  Transistor transistor_2 (.in(transistor_3_out), .out(transistor_2_out), .gate(C));
  Transistor transistor_3 (.in(transistor_4_out), .out(transistor_3_out), .gate(B));
  Transistor transistor_4 (.in(1'b0), .out(transistor_4_out), .gate(A));
  Transistor #(.\type ("n")) transistor_5 (.in(1'b1), .out(out_5), .gate(A));
  Transistor #(.\type ("n")) transistor_6 (.in(1'b1), .out(out_5), .gate(B));
  Transistor #(.\type ("n")) transistor_7 (.in(1'b1), .out(out_5), .gate(C));
  Transistor #(.\type ("n")) transistor_8 (.in(1'b1), .out(out_5), .gate(D));

  // Notes on the sheet:
  //   Fig. 4-Inputt OR Gate
endmodule

module \xnor  (
  input  in_1,
  input  in_2,
  output out_3
);

  wire transistor_1_out, transistor_3_out;

  Transistor transistor_1 (.in(1'b1), .out(transistor_1_out), .gate(in_1));
  Transistor #(.\type ("n")) transistor_2 (.in(1'b0), .out(transistor_1_out), .gate(in_1));
  Transistor transistor_3 (.in(in_1), .out(transistor_3_out), .gate(in_2));
  Transistor #(.\type ("n")) transistor_4 (.in(transistor_1_out), .out(transistor_3_out), .gate(in_2));
  Transistor transistor_5 (.in(1'b1), .out(out_3), .gate(transistor_3_out));
  Transistor #(.\type ("n")) transistor_6 (.in(1'b0), .out(out_3), .gate(transistor_3_out));

  // Notes on the sheet:
  //   Fig. XNOR Gate
endmodule
