// Logisim project p1.circ as structural Verilog: 1 circuit, main circuit main
module main (
  input  in_1,
  input  in_2,
  input  in_3,
  input  in_4,
  output _4_PMOS,
  output _4_NMOS
);

  wire transistor_1_out, transistor_2_out, transistor_3_out, transistor_5_out, transistor_6_out,
       transistor_7_out;

  Transistor #(.\type ("n")) transistor_1 (.in(1'b1), .out(transistor_1_out), .gate(in_1));
  Transistor #(.\type ("n")) transistor_2 (.in(transistor_1_out), .out(transistor_2_out), .gate(in_2));
  Transistor #(.\type ("n")) transistor_3 (.in(transistor_2_out), .out(transistor_3_out), .gate(in_3));
  Transistor #(.\type ("n")) transistor_4 (.in(transistor_3_out), .out(_4_NMOS), .gate(in_4));
  Pull_Resistor pull_resistor_1 (.node(_4_NMOS));
  Transistor transistor_5 (.in(1'b1), .out(transistor_5_out), .gate(in_1));
  Transistor transistor_6 (.in(transistor_5_out), .out(transistor_6_out), .gate(in_2));
  Transistor transistor_7 (.in(transistor_6_out), .out(transistor_7_out), .gate(in_3));
  Transistor transistor_8 (.in(transistor_7_out), .out(_4_PMOS), .gate(in_4));
  Pull_Resistor pull_resistor_2 (.node(_4_PMOS));

  // Other names for the same wires on the sheet: A = in_1; B = in_2; C = in_3; D = in_4

  // Notes on the sheet:
  //   4-NMOS in series 
  //   4-PMOS in series
endmodule
