// Logisim project p2.circ as structural Verilog: 1 circuit, main circuit main
module main (
  input  in_1,
  input  in_2,
  input  in_3,
  input  in_4,
  input  in_5,
  output NAND,
  output AND,
  output NOR,
  output OR
);

  wire transistor_2_out, transistor_3_out, transistor_4_out, transistor_5_out, transistor_12_out,
       transistor_13_out, transistor_14_out, transistor_15_out;

  Pull_Resistor #(.pull(1)) pull_resistor_1 (.node(NAND));
  Transistor #(.\type ("n")) transistor_1 (.in(transistor_2_out), .out(NAND), .gate(in_1));
  Transistor #(.\type ("n")) transistor_2 (.in(transistor_3_out), .out(transistor_2_out), .gate(in_2));
  Transistor #(.\type ("n")) transistor_3 (.in(transistor_4_out), .out(transistor_3_out), .gate(in_3));
  Transistor #(.\type ("n")) transistor_4 (.in(transistor_5_out), .out(transistor_4_out), .gate(in_4));
  Transistor #(.\type ("n")) transistor_5 (.in(1'b0), .out(transistor_5_out), .gate(in_5));
  Transistor #(.\type ("n")) transistor_6 (.in(1'b0), .out(NOR), .gate(in_1));
  Pull_Resistor #(.pull(1)) pull_resistor_2 (.node(NOR));
  Transistor #(.\type ("n")) transistor_7 (.in(1'b0), .out(NOR), .gate(in_2));
  Transistor #(.\type ("n")) transistor_8 (.in(1'b0), .out(NOR), .gate(in_4));
  Transistor #(.\type ("n")) transistor_9 (.in(1'b0), .out(NOR), .gate(in_3));
  Transistor #(.\type ("n")) transistor_10 (.in(1'b0), .out(NOR), .gate(in_5));
  Pull_Resistor pull_resistor_3 (.node(AND));
  Transistor #(.\type ("n")) transistor_11 (.in(transistor_12_out), .out(AND), .gate(in_1));
  Transistor #(.\type ("n")) transistor_12 (.in(transistor_13_out), .out(transistor_12_out), .gate(in_2));
  Transistor #(.\type ("n")) transistor_13 (.in(transistor_14_out), .out(transistor_13_out), .gate(in_3));
  Transistor #(.\type ("n")) transistor_14 (.in(transistor_15_out), .out(transistor_14_out), .gate(in_4));
  Transistor #(.\type ("n")) transistor_15 (.in(1'b1), .out(transistor_15_out), .gate(in_5));
  Transistor #(.\type ("n")) transistor_16 (.in(1'b1), .out(OR), .gate(in_1));
  Pull_Resistor pull_resistor_4 (.node(OR));
  Transistor #(.\type ("n")) transistor_17 (.in(1'b1), .out(OR), .gate(in_2));
  Transistor #(.\type ("n")) transistor_18 (.in(1'b1), .out(OR), .gate(in_3));
  Transistor #(.\type ("n")) transistor_19 (.in(1'b1), .out(OR), .gate(in_4));
  Transistor #(.\type ("n")) transistor_20 (.in(1'b1), .out(OR), .gate(in_5));

  // Other names for the same wires on the sheet: A = in_1; B = in_2; C = in_3; D = in_4; E = in_5

  // Notes on the sheet:
  //   5-Input NAND Gate
  //   5-Input NOR Gate
  //   5-Input AND Gate
  //   5-Input OR Gate
endmodule
