// Logisim project p3.circ as structural Verilog: 1 circuit, main circuit main
module main (
  input  in_1,
  input  in_2,
  input  in_3,
  input  in_4,
  input  in_5,
  output out_6
);

  wire transistor_1_out, transistor_2_out, transistor_4_out, transistor_9_out;

  Transistor transistor_1 (.in(1'b1), .out(transistor_1_out), .gate(in_1));
  Transistor transistor_2 (.in(transistor_1_out), .out(transistor_2_out), .gate(in_3));
  Transistor #(.\type ("n")) transistor_3 (.in(transistor_4_out), .out(out_6), .gate(in_1));
  Transistor #(.\type ("n")) transistor_4 (.in(1'b0), .out(transistor_4_out), .gate(in_2));
  Transistor transistor_5 (.in(1'b1), .out(transistor_1_out), .gate(in_2));
  Transistor transistor_6 (.in(transistor_1_out), .out(transistor_2_out), .gate(in_4));
  Transistor transistor_7 (.in(transistor_2_out), .out(out_6), .gate(in_5));
  Transistor #(.\type ("n")) transistor_8 (.in(transistor_9_out), .out(out_6), .gate(in_3));
  Transistor #(.\type ("n")) transistor_9 (.in(1'b0), .out(transistor_9_out), .gate(in_4));
  Transistor #(.\type ("n")) transistor_10 (.in(1'b0), .out(out_6), .gate(in_5));

  // Other names for the same wires on the sheet: A = in_1; B = in_2; C = in_3; D = in_4; E = in_5
endmodule
