// Logisim project p5.circ as structural Verilog: 1 circuit, main circuit main
module main (
  input  A,
  input  B,
  input  C,
  output AB___C
);

  wire and3_1_output;

  and3 and3_1 (.X(A), .Y(B), .Z(1'b1), .Output(and3_1_output));
  or4 or4_1 (.A(and3_1_output), .B(C), .C(1'b0), .D(1'b0), .out_5(AB___C));
endmodule
