// Logisim project p6.circ as structural Verilog: 1 circuit, main circuit main
module main (
  input  A,
  input  B,
  input  C,
  input  D,
  output A___BC___D
);

  wire and3_1_output;

  and3 and3_1 (.X(B), .Y(1'b1), .Z(C), .Output(and3_1_output));
  or4 or4_1 (.A(A), .B(and3_1_output), .C(1'b0), .D(D), .out_5(A___BC___D));
endmodule
