// Logisim project p7.circ as structural Verilog: 1 circuit, main circuit main
module main (
  input  in_1,
  input  in_2,
  input  in_3,
  input  in_4,
  input  in_5,
  input  in_6,
  output _6AND,
  output _6NOR,
  output _6NAND
);

  wire transistor_8_out, transistor_9_out, transistor_10_out, transistor_11_out, transistor_12_out,
       transistor_15_out, transistor_16_out, transistor_17_out, transistor_18_out, transistor_19_out,
       transistor_32_out, transistor_33_out, transistor_34_out, transistor_35_out, transistor_36_out;

  Transistor transistor_1 (.in(1'b1), .out(_6NAND), .gate(in_1));
  Transistor transistor_2 (.in(1'b1), .out(_6NAND), .gate(in_2));
  Transistor transistor_3 (.in(1'b1), .out(_6NAND), .gate(in_3));
  Transistor transistor_4 (.in(1'b1), .out(_6NAND), .gate(in_4));
  Transistor transistor_5 (.in(1'b1), .out(_6NAND), .gate(in_5));
  Transistor transistor_6 (.in(1'b1), .out(_6NAND), .gate(in_6));
  Transistor #(.\type ("n")) transistor_7 (.in(transistor_8_out), .out(_6NAND), .gate(in_1));
  Transistor #(.\type ("n")) transistor_8 (.in(transistor_9_out), .out(transistor_8_out), .gate(in_2));
  Transistor #(.\type ("n")) transistor_9 (.in(transistor_10_out), .out(transistor_9_out), .gate(in_3));
  Transistor #(.\type ("n")) transistor_10 (.in(transistor_11_out), .out(transistor_10_out), .gate(in_4));
  Transistor #(.\type ("n")) transistor_11 (.in(transistor_12_out), .out(transistor_11_out), .gate(in_5));
  Transistor #(.\type ("n")) transistor_12 (.in(1'b0), .out(transistor_12_out), .gate(in_6));
  Transistor #(.\type ("n")) transistor_13 (.in(1'b0), .out(_6NOR), .gate(in_1));
  Transistor #(.\type ("n")) transistor_14 (.in(1'b0), .out(_6NOR), .gate(in_2));
  Transistor transistor_15 (.in(1'b1), .out(transistor_15_out), .gate(in_1));
  Transistor transistor_16 (.in(transistor_15_out), .out(transistor_16_out), .gate(in_2));
  Transistor transistor_17 (.in(transistor_16_out), .out(transistor_17_out), .gate(in_3));
  Transistor transistor_18 (.in(transistor_17_out), .out(transistor_18_out), .gate(in_4));
  Transistor transistor_19 (.in(transistor_18_out), .out(transistor_19_out), .gate(in_5));
  Transistor transistor_20 (.in(transistor_19_out), .out(_6NOR), .gate(in_6));
  Transistor #(.\type ("n")) transistor_21 (.in(1'b0), .out(_6NOR), .gate(in_3));
  Transistor #(.\type ("n")) transistor_22 (.in(1'b0), .out(_6NOR), .gate(in_4));
  Transistor #(.\type ("n")) transistor_23 (.in(1'b0), .out(_6NOR), .gate(in_5));
  Transistor #(.\type ("n")) transistor_24 (.in(1'b0), .out(_6NOR), .gate(in_6));
  Transistor transistor_25 (.in(1'b0), .out(_6AND), .gate(in_1));
  Transistor transistor_26 (.in(1'b0), .out(_6AND), .gate(in_2));
  Transistor transistor_27 (.in(1'b0), .out(_6AND), .gate(in_3));
  Transistor transistor_28 (.in(1'b0), .out(_6AND), .gate(in_4));
  Transistor transistor_29 (.in(1'b0), .out(_6AND), .gate(in_5));
  Transistor transistor_30 (.in(1'b0), .out(_6AND), .gate(in_6));
  Transistor #(.\type ("n")) transistor_31 (.in(transistor_32_out), .out(_6AND), .gate(in_1));
  Transistor #(.\type ("n")) transistor_32 (.in(transistor_33_out), .out(transistor_32_out), .gate(in_2));
  Transistor #(.\type ("n")) transistor_33 (.in(transistor_34_out), .out(transistor_33_out), .gate(in_3));
  Transistor #(.\type ("n")) transistor_34 (.in(transistor_35_out), .out(transistor_34_out), .gate(in_4));
  Transistor #(.\type ("n")) transistor_35 (.in(transistor_36_out), .out(transistor_35_out), .gate(in_5));
  Transistor #(.\type ("n")) transistor_36 (.in(1'b1), .out(transistor_36_out), .gate(in_6));

  // Other names for the same wires on the sheet: A = in_1; B = in_2; C = in_3; D = in_4; E = in_5; F = in_6
endmodule
