// Logisim project p1.circ as structural Verilog: 1 circuit, main circuit main
module main (
  input  w,
  input  x,
  input  y,
  input  z,
  output Y_2
);

  wire and_1_out, and_2_out, and_3_out, and_4_out, w_prime, x_prime, y_prime, z_prime;

  not not_1 (w_prime, w);
  not not_2 (x_prime, x);
  not not_3 (y_prime, y);
  not not_4 (z_prime, z);
  and and_1 (and_1_out, w, x_prime, y_prime);
  and and_2 (and_2_out, y, w_prime, z_prime);
  and and_3 (and_3_out, y, x, z);
  and and_4 (and_4_out, y, x, w);
  or or_1 (Y_2, and_1_out, and_2_out, and_3_out, and_4_out);

  // Other names for the same wires on the sheet: Y_t = Y_2
endmodule
