// Logisim project p4.circ as structural Verilog: 1 circuit, main circuit main
module main (
  input  A,
  input  B,
  input  s3,
  input  C,
  input  s2,
  input  s1,
  input  D,
  input  s0,
  output d_2,
  output i0,
  output i1
);

  wire and_1_out, and_2_out, and_3_out, and_4_out, not_1_out, not_2_out;

  or or_1 (i0, s3, s2);
  or or_2 (i1, s1, s3);
  not not_1 (not_1_out, i1);
  not not_2 (not_2_out, i0);
  and and_1 (and_1_out, A, not_1_out, not_2_out);
  and and_2 (and_2_out, B, not_1_out, i0);
  and and_3 (and_3_out, C, i1, not_2_out);
  and and_4 (and_4_out, D, i1, i0);
  or or_3 (d_2, and_1_out, and_2_out, and_3_out, and_4_out);

  // Notes on the sheet:
  //   Block A
  //   Block B
endmodule
