// Logisim project p5.circ as structural Verilog: 2 circuits, main circuit main
module main (
  input  a3,
  input  b3,
  input  a2,
  input  b2,
  input  a1,
  input  b1,
  input  a0,
  input  b0,
  input  s0,
  output c3,
  output c2,
  output c1,
  output c0
);

  _2_1_Multiplexer u_2_1_multiplexer_1 (.i0(a3), .i1(b3), .s0(s0), .d(c3));
  _2_1_Multiplexer u_2_1_multiplexer_2 (.i0(a2), .i1(b2), .s0(s0), .d(c2));
  _2_1_Multiplexer u_2_1_multiplexer_3 (.i0(a1), .i1(b1), .s0(s0), .d(c1));
  _2_1_Multiplexer u_2_1_multiplexer_4 (.i0(a0), .i1(b0), .s0(s0), .d(c0));

  // Notes on the sheet:
  //   Two 4-bit inputs
endmodule

module _2_1_Multiplexer (
  input  i0,
  input  i1,
  input  s0,
  output d
);

  wire and_1_out, and_2_out, not_1_out;

  not not_1 (not_1_out, s0);
  and and_1 (and_1_out, i0, not_1_out);
  and and_2 (and_2_out, i1, s0);
  or or_1 (d, and_1_out, and_2_out);

  // Notes on the sheet:
  //   2-1 Multiplexer
endmodule
