// Logisim project p6.circ as structural Verilog: 2 circuits, main circuit main
module main (
  input  d3,
  input  c3,
  input  b3,
  input  a3,
  input  d2,
  input  c2,
  input  b2,
  input  a2,
  input  d1,
  input  c1,
  input  b1,
  input  a1,
  input  d0,
  input  c0,
  input  b0,
  input  a0,
  input  in_17,
  input  in_18,
  output e3,
  output e2,
  output e1,
  output e0
);

  wire not_1_out, not_2_out;

  not not_1 (not_1_out, in_17);
  not not_2 (not_2_out, in_18);
  _4_1_Multiplexer u_4_1_multiplexer_1 (.i0(d3), .i1(c3), .i2(b3), .i3(a3), .s0(not_1_out), .s1(not_2_out), .d(e3));
  _4_1_Multiplexer u_4_1_multiplexer_2 (.i0(d0), .i1(c0), .i2(b0), .i3(a0), .s0(in_17), .s1(in_18), .d(e0));
  _4_1_Multiplexer u_4_1_multiplexer_3 (.i0(d2), .i1(c2), .i2(b2), .i3(a2), .s0(not_1_out), .s1(in_18), .d(e2));
  _4_1_Multiplexer u_4_1_multiplexer_4 (.i0(d1), .i1(c1), .i2(b1), .i3(a1), .s0(in_17), .s1(not_2_out), .d(e1));

  // Notes on the sheet:
  //   Four Inputs A,B,C,D
endmodule

module _4_1_Multiplexer (
  input  i0,
  input  i1,
  input  i2,
  input  i3,
  input  s0,
  input  s1,
  output d
);

  wire and_1_out, and_2_out, and_3_out, and_4_out, not_1_out, not_2_out;

  not not_1 (not_1_out, s0);
  not not_2 (not_2_out, s1);
  and and_1 (and_1_out, i0, not_1_out, not_2_out);
  and and_2 (and_2_out, i1, not_1_out, s1);
  and and_3 (and_3_out, i2, s0, not_2_out);
  and and_4 (and_4_out, i3, s0, s1);
  or or_1 (d, and_1_out, and_2_out, and_3_out, and_4_out);

  // Notes on the sheet:
  //   4-1 Multiplexer
endmodule
