// Logisim project p8.circ as structural Verilog: 1 circuit, main circuit main
module main (
  input  in_1,
  input  in_2,
  input  in_3,
  input  in_4,
  input  in_5,
  input  in_6,
  input  in_7,
  input  in_8,
  input  in_9,
  input  in_10,
  input  in_11,
  input  in_12,
  input  in_13,
  input  in_14,
  input  in_15,
  input  in_16,
  input  s0,
  input  s1,
  input  s2,
  input  s3,
  output d
);

  wire and_1_out, and_2_out, and_3_out, and_4_out, and_5_out, and_6_out, and_7_out, and_8_out, and_9_out,
       and_10_out, and_11_out, and_12_out, and_13_out, and_14_out, and_15_out, and_16_out, not_1_out,
       not_2_out, not_3_out, not_4_out;

  not not_1 (not_1_out, s0);
  not not_2 (not_2_out, s1);
  not not_3 (not_3_out, s2);
  not not_4 (not_4_out, s3);
  and and_1 (and_1_out, in_1, not_1_out, not_2_out, not_3_out, not_4_out);
  and and_2 (and_2_out, in_2, not_1_out, not_2_out, not_3_out, s3);
  and and_3 (and_3_out, in_3, not_1_out, not_2_out, s2, not_4_out);
  and and_4 (and_4_out, in_4, not_1_out, not_2_out, s2, s3);
  and and_5 (and_5_out, in_5, not_1_out, s1, not_3_out, not_4_out);
  and and_6 (and_6_out, in_6, not_1_out, s1, not_3_out, s3);
  and and_7 (and_7_out, in_7, not_1_out, s1, s2, not_4_out);
  and and_8 (and_8_out, in_8, not_1_out, s1, s2, s3);
  and and_9 (and_9_out, in_9, s0, not_2_out, not_3_out, not_4_out);
  and and_10 (and_10_out, in_10, s0, not_2_out, not_3_out, s3);
  and and_11 (and_11_out, in_11, s0, not_2_out, s2, not_4_out);
  and and_12 (and_12_out, in_12, s0, not_2_out, s2, s3);
  and and_13 (and_13_out, in_13, s0, s1, not_3_out, not_4_out);
  and and_14 (and_14_out, in_14, s0, s1, not_3_out, s3);
  and and_15 (and_15_out, in_15, s0, s1, s2, not_4_out);
  and and_16 (and_16_out, in_16, s0, s1, s2, s3);
  or or_1 (d, and_1_out, and_2_out, and_3_out, and_4_out, and_5_out, and_6_out, and_7_out, and_8_out, and_9_out, and_10_out, and_11_out, and_12_out, and_13_out, and_14_out, and_15_out, and_16_out);

  // Notes on the sheet:
  //   16-1 Multiplexer
endmodule
