// Logisim project p9.circ as structural Verilog: 3 circuits, main circuit main
module main (
  input  a0,
  input  b0,
  input  a1,
  input  b1,
  output S0,
  output S1,
  output C
);

  wire ha_1_carry;

  HA ha_1 (.A(a0), .B(b0), .Sum(S0), .Carry(ha_1_carry));
  FA fa_1 (.in_1(ha_1_carry), .in_2(a1), .in_3(b1), .Sum(S1), .Carry(C));
endmodule

module HA (
  input  A,
  input  B,
  output Sum,
  output Carry
);

  xor xor_1 (Sum, A, B);
  and and_1 (Carry, A, B);
endmodule

module FA (
  input  in_1,
  input  in_2,
  input  in_3,
  output Sum,
  output Carry
);

  wire and_1_out, and_2_out, and_3_out, xor_1_out;

  and and_1 (and_1_out, in_1, in_2);
  and and_2 (and_2_out, in_2, in_3);
  and and_3 (and_3_out, in_1, in_3);
  or or_1 (Carry, and_1_out, and_2_out, and_3_out);
  xor xor_1 (xor_1_out, in_1, in_2);
  xor xor_2 (Sum, xor_1_out, in_3);
endmodule
