// Logisim project p1.circ as structural Verilog: 6 circuits, main circuit main
module main (
  input  [3:0] A,
  input  [3:0] B,
  input  [1:0] Selector,
  output [3:0] Output,
  output Carry_in_case_of__adder_and_subtractor_only
);

  _4_bit_ALU u_4_bit_alu_1 (
    .A(A), .B(B), .Selector(Selector), .Carry(Carry_in_case_of__adder_and_subtractor_only), .Output(Output));

  // Notes on the sheet:
  //   Selector  Function
  //   00            A+B
  //   01           A-B
  //   10            A and B
  //   11            A or B
  //   4-bit ALU
endmodule

module FA (
  input  A,
  input  B,
  input  C,
  output Sum,
  output Carry
);

  wire and_1_out, and_2_out, xor_1_out;

  xor xor_1 (xor_1_out, A, B);
  and and_1 (and_1_out, C, xor_1_out);
  and and_2 (and_2_out, A, B);
  xor xor_2 (Sum, xor_1_out, C);
  or or_1 (Carry, and_1_out, and_2_out);
endmodule

module _4_bit_AND (
  input  A0,
  input  B0,
  input  A1,
  input  B1,
  input  A2,
  input  B2,
  input  A3,
  input  B3,
  output S0,
  output S1,
  output S2,
  output S3
);

  and and_1 (S0, A0, B0);
  and and_2 (S1, A1, B1);
  and and_3 (S2, A2, B2);
  and and_4 (S3, A3, B3);
endmodule

module _4_bit_OR (
  input  A0,
  input  B0,
  input  A1,
  input  B1,
  input  A2,
  input  B2,
  input  A3,
  input  B3,
  output S0,
  output S1,
  output S2,
  output S3
);

  or or_1 (S0, A0, B0);
  or or_2 (S1, A1, B1);
  or or_3 (S2, A2, B2);
  or or_4 (S3, A3, B3);
endmodule

module _4_bit_ALU (
  input  [3:0] A,
  input  [3:0] B,
  input  [1:0] Selector,
  output Carry,
  output [3:0] Output
);

  wire [3:0] n4_bit_adder_subtractor_1_s0, n4_bit_and_1_s0, n4_bit_or_1_s0;

  _4_bit_Adder_Subtractor u_4_bit_adder_subtractor_1 (
    .A0(A[0]), .B0(B[0]), .A1(A[1]), .B1(B[1]), .A2(A[2]), .B2(B[2]), .A3(A[3]), .B3(B[3]), .Cout(Carry),
    .Add_0__Sub_1(Selector[0]), .S0(n4_bit_adder_subtractor_1_s0[0]), .S1(n4_bit_adder_subtractor_1_s0[1]),
    .S2(n4_bit_adder_subtractor_1_s0[2]), .S3(n4_bit_adder_subtractor_1_s0[3]));
  _4_bit_AND u_4_bit_and_1 (
    .A0(A[0]), .B0(B[0]), .A1(A[1]), .B1(B[1]), .A2(A[2]), .B2(B[2]), .A3(A[3]), .B3(B[3]),
    .S0(n4_bit_and_1_s0[0]), .S1(n4_bit_and_1_s0[1]), .S2(n4_bit_and_1_s0[2]), .S3(n4_bit_and_1_s0[3]));
  _4_bit_OR u_4_bit_or_1 (
    .A0(A[0]), .B0(B[0]), .A1(A[1]), .B1(B[1]), .A2(A[2]), .B2(B[2]), .A3(A[3]), .B3(B[3]),
    .S0(n4_bit_or_1_s0[0]), .S1(n4_bit_or_1_s0[1]), .S2(n4_bit_or_1_s0[2]), .S3(n4_bit_or_1_s0[3]));
  Multiplexer #(.select(2), .width(4), .enable("false")) multiplexer_1 (
    .in0(n4_bit_adder_subtractor_1_s0), .in1(n4_bit_adder_subtractor_1_s0), .in2(n4_bit_and_1_s0),
    .in3(n4_bit_or_1_s0), .out(Output), .sel(Selector));

  // Other names for the same wires on the sheet: C1 = Selector[0]; C2 = Selector[1]

  // Notes on the sheet:
  //   4-bit ALU
endmodule

module _4_bit_Adder_Subtractor (
  input  Add_0__Sub_1,
  input  A0,
  input  B0,
  input  A1,
  input  B1,
  input  A2,
  input  B2,
  input  A3,
  input  B3,
  output S0,
  output S1,
  output S2,
  output S3,
  output Cout
);

  wire fa_1_carry, fa_2_carry, fa_3_carry, xor_1_out, xor_2_out, xor_3_out, xor_4_out;

  xor xor_1 (xor_1_out, Add_0__Sub_1, B0);
  xor xor_2 (xor_2_out, Add_0__Sub_1, B1);
  xor xor_3 (xor_3_out, Add_0__Sub_1, B2);
  xor xor_4 (xor_4_out, Add_0__Sub_1, B3);
  FA fa_1 (.A(A0), .B(xor_1_out), .C(Add_0__Sub_1), .Sum(S0), .Carry(fa_1_carry));
  FA fa_2 (.A(A1), .B(xor_2_out), .C(fa_1_carry), .Sum(S1), .Carry(fa_2_carry));
  FA fa_3 (.A(A2), .B(xor_3_out), .C(fa_2_carry), .Sum(S2), .Carry(fa_3_carry));
  FA fa_4 (.A(A3), .B(xor_4_out), .C(fa_3_carry), .Sum(S3), .Carry(Cout));
endmodule
