// Logisim project p2.circ as structural Verilog: 4 circuits, main circuit main
module main (
  input  [9:0] A,
  input  [9:0] B,
  output [9:0] A_B,
  output Cout
);

  _10_bit_adder_using_4_bit_adder u_10_bit_adder_using_4_bit_adder_1 (.A(A), .B(B), .A_B(A_B), .Carry(Cout));

  // Notes on the sheet:
  //   10-bit Adder
endmodule

module _4_bit_Adder_Only (
  input  Add_0__Sub_1,
  input  A0,
  input  B0,
  input  A1,
  input  B1,
  input  A2,
  input  B2,
  input  A3,
  input  B3,
  output S0,
  output S1,
  output S2,
  output S3,
  output Cout
);

  wire fa_1_carry, fa_2_carry, fa_3_carry;

  FA fa_1 (.A(A0), .B(B0), .C(Add_0__Sub_1), .Sum(S0), .Carry(fa_1_carry));
  FA fa_2 (.A(A1), .B(B1), .C(fa_1_carry), .Sum(S1), .Carry(fa_2_carry));
  FA fa_3 (.A(A2), .B(B2), .C(fa_2_carry), .Sum(S2), .Carry(fa_3_carry));
  FA fa_4 (.A(A3), .B(B3), .C(fa_3_carry), .Sum(S3), .Carry(Cout));
endmodule

module _10_bit_adder_using_4_bit_adder (
  input  [9:0] A,
  input  [9:0] B,
  output [9:0] A_B,
  output Carry
);

  wire n4_bit_adder_only_1_cout, n4_bit_adder_only_2_cout;

  _4_bit_Adder_Only u_4_bit_adder_only_1 (
    .A0(A[0]), .B0(B[0]), .A1(A[1]), .B1(B[1]), .A2(A[2]), .B2(B[2]), .A3(A[3]), .B3(B[3]),
    .Cout(n4_bit_adder_only_1_cout), .Add_0__Sub_1(1'b0), .S0(A_B[0]), .S1(A_B[1]), .S2(A_B[2]), .S3(A_B[3]));
  _4_bit_Adder_Only u_4_bit_adder_only_2 (
    .A0(A[4]), .B0(B[4]), .A1(A[5]), .B1(B[5]), .A2(A[6]), .B2(B[6]), .A3(A[7]), .B3(B[7]),
    .Cout(n4_bit_adder_only_2_cout), .Add_0__Sub_1(n4_bit_adder_only_1_cout), .S0(A_B[4]), .S1(A_B[5]),
    .S2(A_B[6]), .S3(A_B[7]));
  _4_bit_Adder_Only u_4_bit_adder_only_3 (
    .A0(A[8]), .B0(B[8]), .A1(A[9]), .B1(B[9]), .A2(1'b0), .B2(1'b0), .A3(1'b0), .B3(1'b0),
    .Add_0__Sub_1(n4_bit_adder_only_2_cout), .S0(A_B[8]), .S1(A_B[9]), .S2(Carry));  // open: Cout, S3
endmodule

module FA (
  input  A,
  input  B,
  input  C,
  output Sum,
  output Carry
);

  wire and_1_out, and_2_out, xor_1_out;

  xor xor_1 (xor_1_out, A, B);
  and and_1 (and_1_out, C, xor_1_out);
  and and_2 (and_2_out, A, B);
  xor xor_2 (Sum, xor_1_out, C);
  or or_1 (Carry, and_1_out, and_2_out);
endmodule
