// Logisim project test16.circ as structural Verilog: 2 circuits, main circuit main
module main (
  input  [15:0] A,
  input  [15:0] B,
  input  [3:0] Selector,
  output Flag,
  output [15:0] Output,
  output [15:0] out_6
);

  _16_bit_ALU u_16_bit_alu_1 (.A(A), .B(B), .S(Selector), .F(Flag), .O1(Output), .O2(out_6));

  // Notes on the sheet:
  //   Extra Output in case of :
  //   Multiplication : Most Significant 16-bits
  //   Division : Remainder
endmodule

module _16_bit_ALU (
  input  [15:0] A,
  input  [15:0] B,
  input  [3:0] S,
  output F,
  output [15:0] O1,
  output [15:0] O2
);

  wire and_2_out, comparator_1_lt, not_1_out, not_2_out;
  wire [15:0] adder_1_out, and_1_out, bit_extender_1_out, D2, divider_1_out, M2, multiplier_1_out,
       nand_1_out, nor_1_out, or_1_out, subtractor_1_out, xnor_1_out, xor_1_out;

  Adder #(.width(16)) adder_1 (.a(A), .b(B), .out(adder_1_out), .cin(1'b0));  // open: cout
  Subtractor #(.width(16)) subtractor_1 (.a(A), .b(B), .out(subtractor_1_out), .bin(1'b0));  // open: bout
  Multiplier #(.width(16)) multiplier_1 (.a(A), .b(B), .out(multiplier_1_out), .cin({16{1'b0}}), .cout(M2));
  Divider #(.width(16)) divider_1 (.a(A), .b(B), .out(divider_1_out), .upper({16{1'b0}}), .rem(D2));
  assign and_1_out = A & B;  // AND_Gate and_1, 16 bits wide
  assign or_1_out = A | B;  // OR_Gate or_1, 16 bits wide
  assign xor_1_out = A ^ B;  // XOR_Gate xor_1, 16 bits wide
  assign nand_1_out = ~(A & B);  // NAND_Gate nand_1, 16 bits wide
  assign nor_1_out = ~(A | B);  // NOR_Gate nor_1, 16 bits wide
  assign xnor_1_out = ~(A ^ B);  // XNOR_Gate xnor_1, 16 bits wide
  Comparator #(.width(16)) comparator_1 (.a(A), .b(B), .lt(comparator_1_lt));  // open: gt, eq
  assign bit_extender_1_out = {{15{1'b0}}, comparator_1_lt};  // Bit_Extender bit_extender_1
  Multiplexer #(.select(4), .width(16), .enable("false")) multiplexer_1 (
    .in0(adder_1_out), .in1(subtractor_1_out), .in2(multiplier_1_out), .in3(divider_1_out), .in4(and_1_out),
    .in5(or_1_out), .in6(xor_1_out), .in7(nand_1_out), .in8(nor_1_out), .in9(xnor_1_out),
    .in10(bit_extender_1_out), .out(O1), .sel(S));  // open: in11, in12, in13, in14, in15
  Comparator #(.width(16)) comparator_2 (.a({16{1'b0}}), .b(O1), .eq(F));  // open: gt, lt
  Multiplexer #(.width(16)) multiplexer_2 (.in0(M2), .in1(D2), .out(O2), .sel(S[0]), .en(and_2_out));
  and and_2 (and_2_out, S[1], not_2_out, not_1_out);
  not not_1 (not_1_out, S[3]);
  not not_2 (not_2_out, S[2]);

  // Notes on the sheet:
  //   Original Output
  //   Extra Output in case of :
  //   Division : Remainder
  //   Multiplication : Most Significant 16-bits
endmodule
