// Logisim project p0.circ as structural Verilog: 1 circuit, main circuit main
module main (
  input  in_1,
  input  in_2,
  input  in_3,
  input  Preset,
  input  Clear,
  input  Preset_2,
  input  Clear_2,
  input  Enable,
  input  Enable_2,
  input  in_10,
  input  in_11,
  input  in_12,
  input  Preset_3,
  input  Clear_3,
  input  Enable_3,
  input  in_16,
  input  Clear_4,
  input  Enable_4
);

  wire clock_1_out, clock_2_out, clock_3_out, clock_4_out, d_ff_1_q, j_k_ff_1_q, s_r_ff_1_q, t_ff_1_q;

  Clock clock_1 (.out(clock_1_out));
  Clock clock_2 (.out(clock_2_out));
  J_K_Flip_Flop j_k_ff_1 (
    .J(in_1), .clk(clock_2_out), .K(in_2), .Q(j_k_ff_1_q), .preset(Preset), .en(Enable), .reset(Clear));  // open: Qn
  LED led_1 (.in(j_k_ff_1_q));
  T_Flip_Flop t_ff_1 (
    .clk(clock_1_out), .T(in_12), .Q(t_ff_1_q), .preset(Preset_3), .reset(Clear_3), .en(Enable_3));  // open: Qn
  LED led_2 (.in(t_ff_1_q));
  Clock clock_3 (.out(clock_3_out));
  Clock clock_4 (.out(clock_4_out));
  D_Flip_Flop d_ff_1 (
    .clk(clock_3_out), .D(in_3), .Q(d_ff_1_q), .preset(Preset_2), .en(Enable_2), .reset(Clear_2));  // open: Qn
  S_R_Flip_Flop s_r_ff_1 (
    .S(in_10), .clk(clock_4_out), .R(in_11), .Q(s_r_ff_1_q), .preset(in_16), .reset(Clear_4), .en(Enable_4));  // open: Qn
  LED led_3 (.in(d_ff_1_q));
  LED led_4 (.in(s_r_ff_1_q));

  // Notes on the sheet:
  //   Clock
  //   J-K Flipflop
  //   T Flipflop
  //   preset
  //   D Flipflop
  //   SR Flipflop
endmodule
