// Logisim project p1.circ as structural Verilog: 1 circuit, main circuit main
module main (
  input  Enable,
  input  Input,
  output out_3,
  output out_4,
  output out_5,
  output out_6,
  output out_7,
  output out_8,
  output out_9,
  output out_10
);

  wire Clock_Pulse_out;

  Clock Clock_Pulse (.out(Clock_Pulse_out));
  Register #(.width(1)) register_1 (.D(out_4), .en(Enable), .Q(out_3), .clk(Clock_Pulse_out));  // open: clr
  Register #(.width(1)) register_2 (.D(out_5), .en(Enable), .Q(out_4), .clk(Clock_Pulse_out));  // open: clr
  Register #(.width(1)) register_3 (.D(out_6), .en(Enable), .Q(out_5), .clk(Clock_Pulse_out));  // open: clr
  Register #(.width(1)) register_4 (.D(out_7), .en(Enable), .Q(out_6), .clk(Clock_Pulse_out));  // open: clr
  Register #(.width(1)) register_5 (.D(out_8), .en(Enable), .Q(out_7), .clk(Clock_Pulse_out));  // open: clr
  Register #(.width(1)) register_6 (.D(out_9), .en(Enable), .Q(out_8), .clk(Clock_Pulse_out));  // open: clr
  Register #(.width(1)) register_7 (.D(out_10), .en(Enable), .Q(out_9), .clk(Clock_Pulse_out));  // open: clr
  Register #(.width(1)) register_8 (.D(Input), .en(Enable), .Q(out_10), .clk(Clock_Pulse_out));  // open: clr

  // Notes on the sheet:
  //   8-Bit Shift Register
  //   Output
endmodule
