// Logisim project p2.circ as structural Verilog: 1 circuit, main circuit main
module main (
);

  wire clock_1_out, clock_2_out;
  wire [3:0] d_ff_1_q, d_ff_2_q, d_ff_9_q, random_1_out, random_2_out;
  wire [7:4] random_2_out_2;

  Clock clock_1 (.out(clock_1_out));
  Hex_Digit_Display hex_digit_display_1 (.value(random_2_out));  // open: dp
  Hex_Digit_Display hex_digit_display_2 (.value(random_2_out_2));  // open: dp
  Clock clock_2 (.out(clock_2_out));
  Random #(.width(4)) random_1 (.clk(clock_2_out), .out(random_1_out));  // open: next, clr
  Random random_2 (.clk(clock_1_out), .out({random_2_out_2, random_2_out}));  // open: next, clr
  Hex_Digit_Display hex_digit_display_3 (.value(random_1_out));  // open: dp
  D_Flip_Flop d_ff_1 (.clk(clock_1_out), .D(random_2_out[0]), .Q(d_ff_1_q[0]));  // open: Qn, preset, en, reset
  D_Flip_Flop d_ff_2 (.clk(clock_2_out), .D(random_1_out[0]), .Q(d_ff_2_q[0]));  // open: Qn, preset, en, reset
  D_Flip_Flop d_ff_3 (.clk(clock_1_out), .D(random_2_out[1]), .Q(d_ff_1_q[1]));  // open: Qn, preset, en, reset
  Hex_Digit_Display hex_digit_display_4 (.value(d_ff_9_q));  // open: dp
  Hex_Digit_Display hex_digit_display_5 (.value(d_ff_1_q));  // open: dp
  D_Flip_Flop d_ff_4 (.clk(clock_2_out), .D(random_1_out[1]), .Q(d_ff_2_q[1]));  // open: Qn, preset, en, reset
  D_Flip_Flop d_ff_5 (.clk(clock_1_out), .D(random_2_out[2]), .Q(d_ff_1_q[2]));  // open: Qn, preset, en, reset
  D_Flip_Flop d_ff_6 (.clk(clock_2_out), .D(random_1_out[2]), .Q(d_ff_2_q[2]));  // open: Qn, preset, en, reset
  Hex_Digit_Display hex_digit_display_6 (.value(d_ff_2_q));  // open: dp
  D_Flip_Flop d_ff_7 (.clk(clock_1_out), .D(random_2_out[3]), .Q(d_ff_1_q[3]));  // open: Qn, preset, en, reset
  D_Flip_Flop d_ff_8 (.clk(clock_2_out), .D(random_1_out[3]), .Q(d_ff_2_q[3]));  // open: Qn, preset, en, reset
  D_Flip_Flop d_ff_9 (.clk(clock_1_out), .D(random_2_out_2[4]), .Q(d_ff_9_q[0]));  // open: Qn, preset, en, reset
  D_Flip_Flop d_ff_10 (.clk(clock_1_out), .D(random_2_out_2[5]), .Q(d_ff_9_q[1]));  // open: Qn, preset, en, reset
  D_Flip_Flop d_ff_11 (.clk(clock_1_out), .D(random_2_out_2[6]), .Q(d_ff_9_q[2]));  // open: Qn, preset, en, reset
  D_Flip_Flop d_ff_12 (.clk(clock_1_out), .D(random_2_out_2[7]), .Q(d_ff_9_q[3]));  // open: Qn, preset, en, reset

  // Notes on the sheet:
  //   4-Bit PIPO Register
  //   8-Bit PIPO Register
endmodule
