// Logisim project p4.circ as structural Verilog: 1 circuit, main circuit main
module main (
  input  I0,
  input  I1,
  input  I2,
  input  l3,
  input  I4,
  input  I5,
  input  I6,
  input  l7,
  input  shr_in,
  input  Enable,
  input  [1:0] Select_Lines__s1_s0,
  output Q0,
  output Q1,
  output Q2,
  output Q3,
  output Q4,
  output Q5,
  output Q6,
  output Q7
);

  wire clock_1_out, multiplexer_1_out, multiplexer_2_out, multiplexer_3_out, multiplexer_4_out,
       multiplexer_5_out, multiplexer_6_out, multiplexer_7_out, multiplexer_8_out;

  Multiplexer #(.select(2)) multiplexer_1 (
    .in0(Q0), .in1(I0), .in2(Q1), .in3(1'b0), .out(multiplexer_1_out), .sel(Select_Lines__s1_s0));  // open: en
  Multiplexer #(.select(2)) multiplexer_2 (
    .in0(Q1), .in1(I1), .in2(Q2), .in3(1'b0), .out(multiplexer_2_out), .sel(Select_Lines__s1_s0));  // open: en
  Multiplexer #(.select(2)) multiplexer_3 (
    .in0(Q2), .in1(I2), .in2(Q3), .in3(1'b0), .out(multiplexer_3_out), .sel(Select_Lines__s1_s0));  // open: en
  Multiplexer #(.select(2)) multiplexer_4 (
    .in0(Q3), .in1(l3), .in2(Q4), .in3(1'b0), .out(multiplexer_4_out), .sel(Select_Lines__s1_s0));  // open: en
  Multiplexer #(.select(2)) multiplexer_5 (
    .in0(Q4), .in1(I4), .in2(Q5), .in3(1'b0), .out(multiplexer_5_out), .sel(Select_Lines__s1_s0));  // open: en
  Multiplexer #(.select(2)) multiplexer_6 (
    .in0(Q5), .in1(I5), .in2(Q6), .in3(1'b0), .out(multiplexer_6_out), .sel(Select_Lines__s1_s0));  // open: en
  Multiplexer #(.select(2)) multiplexer_7 (
    .in0(Q6), .in1(I6), .in2(Q7), .in3(1'b0), .out(multiplexer_7_out), .sel(Select_Lines__s1_s0));  // open: en
  Multiplexer #(.select(2)) multiplexer_8 (
    .in0(Q7), .in1(l7), .in2(shr_in), .in3(1'b0), .out(multiplexer_8_out), .sel(Select_Lines__s1_s0));  // open: en
  Clock clock_1 (.out(clock_1_out));
  Register #(.width(1)) register_1 (.D(multiplexer_1_out), .en(Enable), .Q(Q0), .clk(clock_1_out));  // open: clr
  Register #(.width(1)) register_2 (.D(multiplexer_2_out), .en(Enable), .Q(Q1), .clk(clock_1_out));  // open: clr
  Register #(.width(1)) register_3 (.D(multiplexer_3_out), .en(Enable), .Q(Q2), .clk(clock_1_out));  // open: clr
  Register #(.width(1)) register_4 (.D(multiplexer_4_out), .en(Enable), .Q(Q3), .clk(clock_1_out));  // open: clr
  Register #(.width(1)) register_5 (.D(multiplexer_5_out), .en(Enable), .Q(Q4), .clk(clock_1_out));  // open: clr
  Register #(.width(1)) register_6 (.D(multiplexer_6_out), .en(Enable), .Q(Q5), .clk(clock_1_out));  // open: clr
  Register #(.width(1)) register_7 (.D(multiplexer_7_out), .en(Enable), .Q(Q6), .clk(clock_1_out));  // open: clr
  Register #(.width(1)) register_8 (.D(multiplexer_8_out), .en(Enable), .Q(Q7), .clk(clock_1_out));  // open: clr

  // Notes on the sheet:
  //   Multi-function Shift Register (8-bit)
endmodule
