// Logisim project register-file.circ as structural Verilog: 2 circuits, main circuit main
module main (
  input  [7:0] Data,
  input  [1:0] WriteAddress,
  input  clk,
  input  [1:0] ReadAdress,
  output [7:0] OutData
);

  wire decoder_1_out0, decoder_1_out1, decoder_1_out2, decoder_1_out3;
  wire [7:0] register_1_q, register_2_q, register_3_q, register_4_q;

  Decoder #(.select(2)) decoder_1 (
    .out0(decoder_1_out0), .out1(decoder_1_out1), .out2(decoder_1_out2), .out3(decoder_1_out3),
    .sel(WriteAddress));  // open: en
  Register register_1 (.D(Data), .en(decoder_1_out0), .Q(register_1_q), .clk(clk));  // open: clr
  Register register_2 (.D(Data), .en(decoder_1_out1), .Q(register_2_q), .clk(clk));  // open: clr
  Register register_3 (.D(Data), .en(decoder_1_out2), .Q(register_3_q), .clk(clk));  // open: clr
  Register register_4 (.D(Data), .en(decoder_1_out3), .Q(register_4_q), .clk(clk));  // open: clr
  Multiplexer #(.select(2), .width(8)) multiplexer_1 (
    .in0(register_1_q), .in1(register_2_q), .in2(register_3_q), .in3(register_4_q), .out(OutData),
    .sel(ReadAdress));  // open: en
endmodule

module Reg_block (
  input  [7:0] in_1,
  input  [1:0] in_2,
  input  [1:0] in_3,
  output [7:0] out_4
);

  wire clock_1_out;

  Clock clock_1 (.out(clock_1_out));
  main main_1 (.Data(in_1), .WriteAddress(in_2), .clk(clock_1_out), .ReadAdress(in_3), .OutData(out_4));
endmodule
