// Logisim project shift-4.circ as structural Verilog: 1 circuit, main circuit main
module main (
  input  in_1,
  input  in_2
);

  wire clock_1_out, clock_2_out;
  wire [3:0] random_1_out, register_1_q, register_2_q, register_3_q, register_4_q;

  Clock clock_1 (.out(clock_1_out));
  Random #(.width(4)) random_1 (.clk(clock_1_out), .out(random_1_out));  // open: next, clr
  Clock clock_2 (.out(clock_2_out));
  Register #(.width(4)) register_1 (.D(random_1_out), .en(in_1), .Q(register_1_q), .clk(clock_2_out));  // open: clr
  Hex_Digit_Display hex_digit_display_1 (.value(register_1_q));  // open: dp
  Register #(.width(4)) register_2 (.D(register_1_q), .Q(register_2_q), .clk(clock_2_out));  // open: en, clr
  Hex_Digit_Display hex_digit_display_2 (.value(register_2_q));  // open: dp
  Register #(.width(4)) register_3 (.D(register_2_q), .Q(register_3_q), .clk(clock_2_out));  // open: en, clr
  Hex_Digit_Display hex_digit_display_3 (.value(register_3_q));  // open: dp
  Register #(.width(4)) register_4 (.D(register_3_q), .Q(register_4_q), .clk(clock_2_out));  // open: en, clr
  Hex_Digit_Display hex_digit_display_4 (.value(register_4_q));  // open: dp
endmodule
