// Logisim project L9Q1_JK.circ as structural Verilog: 1 circuit, main circuit main
module main (
  output C2,
  output C3,
  output C4,
  output C1
);

  wire and_1_out, and_2_out, CLK_out;

  Clock CLK (.out(CLK_out));
  J_K_Flip_Flop j_k_ff_1 (.J(1'b1), .clk(CLK_out), .K(1'b1), .Q(C1));  // open: Qn, preset, en, reset
  J_K_Flip_Flop j_k_ff_2 (.J(C1), .clk(CLK_out), .K(C1), .Q(C2));  // open: Qn, preset, en, reset
  and and_1 (and_1_out, C1, C2);
  J_K_Flip_Flop j_k_ff_3 (.J(and_1_out), .clk(CLK_out), .K(and_1_out), .Q(C3));  // open: Qn, preset, en, reset
  and and_2 (and_2_out, C1, C2, C3);
  J_K_Flip_Flop j_k_ff_4 (.J(and_2_out), .clk(CLK_out), .K(and_2_out), .Q(C4));  // open: Qn, preset, en, reset

  // Notes on the sheet:
  //   Fig. 4-bit JK counter
  //   Current State = C4C3C2C1
endmodule
