// Logisim project L9Q1_Q.circ as structural Verilog: 1 circuit, main circuit main
module main (
  output C4,
  output C3,
  output C1,
  output C2
);

  wire and_1_out, and_2_out, CLK_out, xor_1_out, xor_2_out, xor_3_out, xor_4_out;

  Clock CLK (.out(CLK_out));
  D_Flip_Flop d_ff_1 (.clk(CLK_out), .D(xor_1_out), .Q(C1));  // open: Qn, preset, en, reset
  xor xor_1 (xor_1_out, 1'b1, C1);
  xor xor_2 (xor_2_out, C1, C2);
  D_Flip_Flop d_ff_2 (.clk(CLK_out), .D(xor_2_out), .Q(C2));  // open: Qn, preset, en, reset
  xor xor_3 (xor_3_out, and_1_out, C3);
  and and_1 (and_1_out, C2, C1);
  D_Flip_Flop d_ff_3 (.clk(CLK_out), .D(xor_3_out), .Q(C3));  // open: Qn, preset, en, reset
  xor xor_4 (xor_4_out, and_2_out, C4);
  and and_2 (and_2_out, C3, C1, C2);
  D_Flip_Flop d_ff_4 (.clk(CLK_out), .D(xor_4_out), .Q(C4));  // open: Qn, preset, en, reset

  // Notes on the sheet:
  //   Fig. 4-bit D Counter
  //   Current State = C4C3C2C1
endmodule
