// Logisim project L9Q1_SR.circ as structural Verilog: 1 circuit, main circuit main
module main (
  output C4,
  output C1,
  output C2,
  output C3
);

  wire and_1_out, and_2_out, and_3_out, and_4_out, and_5_out, and_6_out, CLK_out, s_r_ff_1_qn, s_r_ff_2_qn,
       s_r_ff_3_qn, s_r_ff_4_qn;

  Clock CLK (.out(CLK_out));
  S_R_Flip_Flop s_r_ff_1 (.S(s_r_ff_1_qn), .clk(CLK_out), .R(C1), .Q(C1), .Qn(s_r_ff_1_qn));  // open: preset, reset, en
  and and_1 (and_1_out, C1, s_r_ff_2_qn);
  and and_2 (and_2_out, C1, C2);
  S_R_Flip_Flop s_r_ff_2 (
    .S(and_1_out), .clk(CLK_out), .R(and_2_out), .Q(C2), .Qn(s_r_ff_2_qn));  // open: preset, reset, en
  and and_3 (and_3_out, C1, C2, s_r_ff_3_qn);
  and and_4 (and_4_out, C1, C2, C3);
  S_R_Flip_Flop s_r_ff_3 (
    .S(and_3_out), .clk(CLK_out), .R(and_4_out), .Q(C3), .Qn(s_r_ff_3_qn));  // open: preset, reset, en
  and and_5 (and_5_out, C1, C2, C3, s_r_ff_4_qn);
  and and_6 (and_6_out, C1, C2, C3, C4);
  S_R_Flip_Flop s_r_ff_4 (
    .S(and_5_out), .clk(CLK_out), .R(and_6_out), .Q(C4), .Qn(s_r_ff_4_qn));  // open: preset, reset, en

  // Notes on the sheet:
  //   Current State = C4C3C2C1
  //   Fig. 4-bit RS Counter
endmodule
