// Logisim project L9Q1_T.circ as structural Verilog: 1 circuit, main circuit main
module main (
  output C2,
  output C3,
  output C4,
  output C1
);

  wire and_1_out, and_2_out, CLK_out;

  Clock CLK (.out(CLK_out));
  T_Flip_Flop t_ff_1 (.clk(CLK_out), .T(1'b1), .Q(C1));  // open: Qn, preset, reset, en
  T_Flip_Flop t_ff_2 (.clk(CLK_out), .T(C1), .Q(C2));  // open: Qn, preset, reset, en
  and and_1 (and_1_out, C1, C2);
  T_Flip_Flop t_ff_3 (.clk(CLK_out), .T(and_1_out), .Q(C3));  // open: Qn, preset, reset, en
  and and_2 (and_2_out, C1, C2, C3);
  T_Flip_Flop t_ff_4 (.clk(CLK_out), .T(and_2_out), .Q(C4));  // open: Qn, preset, reset, en

  // Notes on the sheet:
  //   Current State = C4C3C2C1
  //   Fig. 4-bit T counter
endmodule
