// Logisim project L9Q3.circ as structural Verilog: 3 circuits, main circuit main
module main (
  input  [3:0] Read_Addr_0,
  input  [3:0] Read_Addr_1,
  input  [3:0] Write_Addr,
  input  [15:0] Write_Value,
  input  [1:0] Opertion_Selector,
  input  Write_Selector,
  input  RegWrite,
  input  RegClear,
  output [15:0] Result
);

  wire Clock_out;
  wire [15:0] multiplexer_1_out, reg_16_bit_1_read_value_0, reg_16_bit_1_read_value_1;

  Multiplexer #(.width(16)) multiplexer_1 (
    .in0(Write_Value), .in1(Result), .out(multiplexer_1_out), .sel(Write_Selector));  // open: en
  Reg_16_bit reg_16_bit_1 (
    .Read_Addr_0(Read_Addr_0), .Read_Addr_1(Read_Addr_1), .Write_Addr(Write_Addr), .RegWrite(RegWrite),
    .CLOCK(Clock_out), .Write_Value(multiplexer_1_out), .Read_Value_0(reg_16_bit_1_read_value_0),
    .Read_Value_1(reg_16_bit_1_read_value_1), .RegClear(RegClear));
  Clock Clock (.out(Clock_out));
  ALU_16_bit alu_16_bit_1 (
    .I1(reg_16_bit_1_read_value_0), .I2(reg_16_bit_1_read_value_1), .Operation_Selector(Opertion_Selector),
    .Output(Result));

  // Notes on the sheet:
  //   16x16 register file
  //   16-bit ALU
  //   Addition 0 0
  //   Subtraction 0 1
  //   Bitwise AND 1 0
  //   Bitwise OR 1 1
endmodule

module ALU_16_bit (
  input  [15:0] I1,
  input  [15:0] I2,
  input  [1:0] Operation_Selector,
  output [15:0] Output
);

  wire [15:0] adder_1_out, and_1_out, or_1_out, subtractor_1_out;

  Adder #(.width(16)) adder_1 (.a(I1), .b(I2), .out(adder_1_out), .cin(1'b0));  // open: cout
  Subtractor #(.width(16)) subtractor_1 (.a(I1), .b(I2), .out(subtractor_1_out), .bin(1'b0));  // open: bout
  assign and_1_out = I1 & I2;  // AND_Gate and_1, 16 bits wide
  assign or_1_out = I1 | I2;  // OR_Gate or_1, 16 bits wide
  Multiplexer #(.select(2), .width(16), .enable("false")) multiplexer_1 (
    .in0(adder_1_out), .in1(subtractor_1_out), .in2(and_1_out), .in3(or_1_out), .out(Output),
    .sel(Operation_Selector));

  // Notes on the sheet:
  //   Fig. ALU 16-bit
endmodule

module Reg_16_bit (
  input  [3:0] Read_Addr_0,
  input  [3:0] Read_Addr_1,
  input  [3:0] Write_Addr,
  input  [15:0] Write_Value,
  input  RegWrite,
  input  CLOCK,
  input  RegClear,
  output [15:0] Read_Value_0,
  output [15:0] Read_Value_1
);

  wire and_1_out, and_2_out, and_3_out, and_4_out, and_5_out, and_6_out, and_7_out, and_8_out, and_9_out,
       and_10_out, and_11_out, and_12_out, and_13_out, and_14_out, and_15_out, and_16_out, decoder_1_out0,
       decoder_1_out1, decoder_1_out2, decoder_1_out3, decoder_1_out4, decoder_1_out5, decoder_1_out6,
       decoder_1_out7, decoder_1_out8, decoder_1_out9, decoder_1_out10, decoder_1_out11, decoder_1_out12,
       decoder_1_out13, decoder_1_out14, decoder_1_out15;
  wire [15:0] register_1_q, register_2_q, register_3_q, register_4_q, register_5_q, register_6_q,
       register_7_q, register_8_q, register_9_q, register_10_q, register_11_q, register_12_q, register_13_q,
       register_14_q, register_15_q, register_16_q;

  Decoder #(.select(4)) decoder_1 (
    .out0(decoder_1_out0), .out1(decoder_1_out1), .out2(decoder_1_out2), .out3(decoder_1_out3),
    .out4(decoder_1_out4), .out5(decoder_1_out5), .out6(decoder_1_out6), .out7(decoder_1_out7),
    .out8(decoder_1_out8), .out9(decoder_1_out9), .out10(decoder_1_out10), .out11(decoder_1_out11),
    .out12(decoder_1_out12), .out13(decoder_1_out13), .out14(decoder_1_out14), .out15(decoder_1_out15),
    .sel(Write_Addr));  // open: en
  and and_1 (and_1_out, RegWrite, decoder_1_out0);
  and and_2 (and_2_out, RegWrite, decoder_1_out1);
  and and_3 (and_3_out, RegWrite, decoder_1_out2);
  and and_4 (and_4_out, RegWrite, decoder_1_out3);
  and and_5 (and_5_out, RegWrite, decoder_1_out4);
  and and_6 (and_6_out, RegWrite, decoder_1_out5);
  and and_7 (and_7_out, RegWrite, decoder_1_out6);
  and and_8 (and_8_out, RegWrite, decoder_1_out7);
  and and_9 (and_9_out, RegWrite, decoder_1_out8);
  and and_10 (and_10_out, RegWrite, decoder_1_out9);
  and and_11 (and_11_out, RegWrite, decoder_1_out10);
  and and_12 (and_12_out, RegWrite, decoder_1_out11);
  and and_13 (and_13_out, RegWrite, decoder_1_out12);
  and and_14 (and_14_out, RegWrite, decoder_1_out13);
  and and_15 (and_15_out, decoder_1_out14, RegWrite);
  and and_16 (and_16_out, decoder_1_out15, RegWrite);
  Register #(.width(16)) register_1 (.D(Write_Value), .en(and_1_out), .Q(register_1_q), .clk(CLOCK), .clr(RegClear));
  Register #(.width(16)) register_2 (.D(Write_Value), .en(and_2_out), .Q(register_2_q), .clk(CLOCK), .clr(RegClear));
  Register #(.width(16)) register_3 (.D(Write_Value), .en(and_3_out), .Q(register_3_q), .clk(CLOCK), .clr(RegClear));
  Register #(.width(16)) register_4 (.D(Write_Value), .en(and_4_out), .Q(register_4_q), .clk(CLOCK), .clr(RegClear));
  Register #(.width(16)) register_5 (.D(Write_Value), .en(and_5_out), .Q(register_5_q), .clk(CLOCK), .clr(RegClear));
  Register #(.width(16)) register_6 (.D(Write_Value), .en(and_6_out), .Q(register_6_q), .clk(CLOCK), .clr(RegClear));
  Register #(.width(16)) register_7 (.D(Write_Value), .en(and_7_out), .Q(register_7_q), .clk(CLOCK), .clr(RegClear));
  Register #(.width(16)) register_8 (.D(Write_Value), .en(and_8_out), .Q(register_8_q), .clk(CLOCK), .clr(RegClear));
  Register #(.width(16)) register_9 (.D(Write_Value), .en(and_9_out), .Q(register_9_q), .clk(CLOCK), .clr(RegClear));
  Register #(.width(16)) register_10 (.D(Write_Value), .en(and_10_out), .Q(register_10_q), .clk(CLOCK), .clr(RegClear));
  Register #(.width(16)) register_11 (.D(Write_Value), .en(and_11_out), .Q(register_11_q), .clk(CLOCK), .clr(RegClear));
  Register #(.width(16)) register_12 (.D(Write_Value), .en(and_12_out), .Q(register_12_q), .clk(CLOCK), .clr(RegClear));
  Register #(.width(16)) register_13 (.D(Write_Value), .en(and_13_out), .Q(register_13_q), .clk(CLOCK), .clr(RegClear));
  Register #(.width(16)) register_14 (.D(Write_Value), .en(and_14_out), .Q(register_14_q), .clk(CLOCK), .clr(RegClear));
  Register #(.width(16)) register_15 (.D(Write_Value), .en(and_15_out), .Q(register_15_q), .clk(CLOCK), .clr(RegClear));
  Register #(.width(16)) register_16 (.D(Write_Value), .en(and_16_out), .Q(register_16_q), .clk(CLOCK), .clr(RegClear));
  Multiplexer #(.select(4), .width(16)) multiplexer_1 (
    .in0(register_1_q), .in1(register_2_q), .in2(register_3_q), .in3(register_4_q), .in4(register_5_q),
    .in5(register_6_q), .in6(register_7_q), .in7(register_8_q), .in8(register_9_q), .in9(register_10_q),
    .in10(register_11_q), .in11(register_12_q), .in12(register_13_q), .in13(register_14_q),
    .in14(register_15_q), .in15(register_16_q), .out(Read_Value_0), .sel(Read_Addr_0));  // open: en
  Multiplexer #(.select(4), .width(16)) multiplexer_2 (
    .in0(register_1_q), .in1(register_2_q), .in2(register_3_q), .in3(register_4_q), .in4(register_5_q),
    .in5(register_6_q), .in6(register_7_q), .in7(register_8_q), .in8(register_9_q), .in9(register_10_q),
    .in10(register_11_q), .in11(register_12_q), .in12(register_13_q), .in13(register_14_q),
    .in14(register_15_q), .in15(register_16_q), .out(Read_Value_1), .sel(Read_Addr_1));  // open: en
endmodule
