// Logisim project 3bit-RS-counter.circ as structural Verilog: 1 circuit, main circuit main
module main (
  output out_1,
  output out_2,
  output out_3
);

  wire and_1_out, and_2_out, and_3_out, and_4_out, and_5_out, clock_1_out, s_r_ff_1_qn, s_r_ff_2_qn,
       s_r_ff_3_qn;

  Clock clock_1 (.out(clock_1_out));
  S_R_Flip_Flop s_r_ff_1 (
    .S(s_r_ff_1_qn), .clk(clock_1_out), .R(out_2), .Q(out_2), .Qn(s_r_ff_1_qn));  // open: preset, reset, en
  and and_1 (and_1_out, s_r_ff_2_qn, out_2);
  and and_2 (and_2_out, out_2, out_3);
  and and_3 (and_3_out, out_2, out_3);
  S_R_Flip_Flop s_r_ff_2 (
    .S(and_1_out), .clk(clock_1_out), .R(and_2_out), .Q(out_3), .Qn(s_r_ff_2_qn));  // open: preset, reset, en
  and and_4 (and_4_out, s_r_ff_3_qn, and_3_out);
  and and_5 (and_5_out, and_3_out, out_1);
  S_R_Flip_Flop s_r_ff_3 (
    .S(and_4_out), .clk(clock_1_out), .R(and_5_out), .Q(out_1), .Qn(s_r_ff_3_qn));  // open: preset, reset, en
endmodule
